// Logisim project NS.circ as structural Verilog: 3 circuits, main circuit main
module main (
  input  N2,
  input  N1,
  input  N0,
  output P
);

  wire and_1_out, not_1_out;

  not not_1 (not_1_out, N2);
  and and_1 (and_1_out, not_1_out, N1);
  or or_1 (P, and_1_out, N0);
endmodule

module contador_for (
  input  in_1,
  input  in_2
);


  // Notes on the sheet:
  //   00000000001010
  //   X
  //   Y
  //   Alu
  //   S
  //   00000010010100
endmodule

module If (
  input  A,
  input  B,
  output X,
  output Y
);

  wire not_1_out, not_2_out;

  or or_1 (X, B, A);
  not not_1 (not_1_out, A);
  not not_2 (not_2_out, B);
  and and_1 (Y, not_1_out, not_2_out);
endmodule
